# Fritzing sketch RFIDSound (saved by Fritzing 0.9.3b)
breadboards: 1

parts:
  Part1 = Arduino Nano (Rev3.0)
  Part2 = Arduino Uno (Rev3)
  Part3 = RFID-RC522-v3
  Part4 = MicroSD Card Module
  Part5 = Audio Jack Breakout

nets:
  GND: Part1.GND, Part4.GND, Part5.GND
  N1: Part1.D8, Part4.CS
  N2: Part1.D9, Part5.TIP
  N3: Part1.D11/MOSI, Part4.MOSI
  N4: Part1.D12/MISO, Part4.MISO
  VIN: Part1.VIN, Part2.5V
  5V: Part1.5V, Part4.VCC
  N5: Part1.A5, Part2.A5/SCL
  N6: Part1.A4, Part2.A4/SDA
  N7: Part1.D13/SCK, Part4.SCK
  N8: Part2.D9_PWM, Part3.RST
  N9: Part2.D10_PWM/SS, Part3.SDA
  N10: Part2.D11_PWM/MOSI, Part3.MOSI
  N11: Part2.D12/MISO, Part3.MISO
  N12: Part2.D13/SCK, Part3.SCK
  3V3: Part2.3V3, Part3.3.3V
  GND_2: Part2.GND, Part3.GND

custom parts:
  RFID-RC522-v3: A simple China made RFID-RC522 Reader (6x4 cm); do check the pin labels, as this is a MFRC522 based clone.
