# Fritzing sketch RFIDSound4Relay (saved by Fritzing 0.9.3b)
breadboards: 1

parts:
  Part1 = Arduino Nano (Rev3.0)
  Part2 = Arduino Uno (Rev3)
  Part3 = RFID-RC522-v3
  Part4 = MicroSD Card Module
  Part5 = Audio Jack Breakout
  U1 = 4-Channel 5v Relay Shield [package=relay-4ch5v10a]

nets:
  GND: Part1.GND, Part4.GND, Part5.GND
  N1: Part1.D8, Part4.CS
  N2: Part1.D9, Part5.TIP
  N3: Part1.D11/MOSI, Part4.MOSI
  N4: Part1.D12/MISO, Part4.MISO
  VIN: Part1.VIN, Part2.5V, U1.VCC
  5V: Part1.5V, Part4.VCC
  N5: Part1.A5, Part2.A5/SCL
  N6: Part1.A4, Part2.A4/SDA
  N7: Part1.D13/SCK, Part4.SCK
  N8: Part2.D10_PWM/SS, Part3.SDA
  N9: Part2.D11_PWM/MOSI, Part3.MOSI
  N10: Part2.D12/MISO, Part3.MISO
  N11: Part2.D13/SCK, Part3.SCK
  GND_2: Part2.GND, Part3.GND, U1.GND
  N12: Part2.D4, U1.IN4
  N13: Part2.D5_PWM, U1.IN3
  N14: Part2.D6_PWM, U1.IN2
  N15: Part2.D7, U1.IN1
  3V3: Part2.3V3, Part3.3.3V

custom parts:
  RFID-RC522-v3: A simple China made RFID-RC522 Reader (6x4 cm); do check the pin labels, as this is a MFRC522 based clone.
  4-Channel 5v Relay Shield: 4 Channel 5v Relay Shield w. 2x SPD-06VDC-SD-C
